# Fritzing sketch cmafzz (saved by Fritzing 0.9.3b)
breadboards: 3

parts:
  Componente1 = Arduino Ethernet Shield (Rev3)
  Componente2 = Arduino Mega 2560 (Rev3)
  RHT1 = Humidity and Temperature Sensor RHT03
  RHT2 = Humidity and Temperature Sensor RHT03
  U1 = GAS_SENSOR [package=mq-3]
  U2 = GAS_SENSOR [package=mq-3]
  R1 = Resistor [tolerance=±5% resistance=220 package="0603 [SMD]"]
  R2 = Resistor [tolerance=±5% resistance=220 package="0603 [SMD]"]
  LED1 = LED - 3mm [color="Red (633nm)" package="3 mm [THT]"]
  LED2 = LED - 3mm [color="Red (633nm)" package="3 mm [THT]"]
  R3 = Resistor [tolerance=±5% resistance=220 package="0603 [SMD]"]
  R4 = Resistor [tolerance=±5% resistance=220 package="0603 [SMD]"]
  R5 = Resistor [tolerance=±5% resistance=220 package="0603 [SMD]"]
  LED3 = LED - 3mm [color="Red (633nm)" package="3 mm [THT]"]
  R6 = Resistor [tolerance=±5% resistance=220 package="0603 [SMD]"]
  LED4 = LED - 3mm [color="Red (633nm)" package="3 mm [THT]"]
  LED5 = LED - 3mm [color="Red (633nm)" package="3 mm [THT]"]
  LED6 = LED - 3mm [color="Red (633nm)" package="3 mm [THT]"]
  LED7 = LED - 3mm [color="Red (633nm)" package="3 mm [THT]"]
  LED8 = LED - 3mm [color="Red (633nm)" package="3 mm [THT]"]
  R7 = Resistor [tolerance=±5% resistance=220 package="0603 [SMD]"]
  R8 = Resistor [tolerance=±5% resistance=220 package="0603 [SMD]"]
  R9 = Resistor [tolerance=±5% resistance=220 package="0603 [SMD]"]
  R10 = Resistor [tolerance=±5% resistance=220 package="0603 [SMD]"]
  U3 = LCD-16X2 [package=lcd-16x2_nosilk]
  Componente3 = Arduino Uno (Rev3)
  U4 = GAS_SENSOR [package=mq-3]
  R11 = Resistor [tolerance=±5% resistance=220 package="0603 [SMD]"]
  R12 = Resistor [tolerance=±5% resistance=220 package="0603 [SMD]"]
  R13 = Resistor [tolerance=±5% resistance=220 package="0603 [SMD]"]
  LED9 = LED - 3mm [color="Red (633nm)" package="3 mm [THT]"]
  LED10 = LED - 3mm [color="Red (633nm)" package="3 mm [THT]"]
  U5 = POT [package=pot_alpha_rv16af-20]

nets:
  N1: Componente1.ETH_CS, Componente3.D1/TX
  N2: Componente1.PWM_D11, Componente3.D0/RX
  GND: Componente1.GND, RHT1.GND_2, RHT2.GND_2, U1.H1, U2.H1, R3.Pin_0, R4.Pin_0, R5.Pin_0, R6.Pin_0, R7.Pin_1, R8.Pin_1, R9.Pin_1, R10.Pin_1, U3.VSS, U3.R_W, U3.K, Componente3.GND, U4.H1, R12.Pin_0, R13.Pin_0, U5.E
  N3: Componente2.A8, R1.Pin_0
  N4: Componente2.A9, R2.Pin_0
  N5: Componente2.A10, R11.Pin_0
  N6: Componente2.D21/SCL, LED3.anode
  N7: Componente2.D20/SDA, LED1.anode
  N8: Componente2.D19/RX1, LED4.anode
  N9: Componente2.D18/TX1, LED2.anode
  N10: Componente2.D17_PWM/RX2, LED5.anode
  N11: Componente2.D16_PWM/TX2, LED6.anode
  N12: Componente2.D15/RX3, LED7.anode
  N13: Componente2.D14/TX3, LED8.anode
  VCC: Componente2.5V, RHT1.Vcc, RHT2.Vcc, U1.H2, U2.H2
  N14: Componente2.D22, RHT1.Data-signal
  N15: Componente2.D24, RHT2.Data-signal
  N16: Componente2.D26, LED9.anode
  N17: Componente2.D28, LED10.anode
  N18: U1.B1, R1.Pin_1
  N19: U2.B1, R2.Pin_1
  N20: LED1.cathode, R3.Pin_1
  N21: LED2.cathode, R4.Pin_1
  N22: R5.Pin_1, LED3.cathode
  N23: R6.Pin_1, LED4.cathode
  N24: LED5.cathode, R8.Pin_0
  N25: LED6.cathode, R7.Pin_0
  N26: LED7.cathode, R9.Pin_0
  N27: LED8.cathode, R10.Pin_0
  VDD: U3.VDD, U3.A, Componente3.5V, U5.A
  N28: U3.VO, U5.S
  N29: U3.RS, Componente3.D8
  N30: U3.E, Componente3.D9_PWM
  N31: U3.DB4, Componente3.D7
  N32: U3.DB5, Componente3.D6_PWM
  N33: U3.DB6, Componente3.D5_PWM
  N34: U3.DB7, Componente3.D4
  N35: U4.B1, R11.Pin_1
  N36: R12.Pin_1, LED9.cathode
  N37: R13.Pin_1, LED10.cathode
